# Fritzing sketch push_button_if_statement_example (saved by Fritzing 0.9.0b)
breadboards: 1

parts:
  S1 = Pushbutton [package="[THT]"]
  R1 = Resistor [tolerance=±5% resistance=220 package=THT]
  Part1 = Arduino Uno (Rev3)
  LED1 = LED - 5mm [color="Red (633nm)" package="5 mm [THT]"]

nets:
  N1: S1.Pin_1, S1.Pin_2
  N2: S1.Pin_3, S1.Pin_4, R1.Pin_1, LED1.anode
  N3: R1.Pin_0, Part1.5V
  N4: Part1.GND, LED1.cathode
