# Fritzing sketch push_button_or_statement_example (saved by Fritzing 0.9.0b)
breadboards: 1

parts:
  Part1 = Arduino Uno (Rev3)
  R1 = Resistor [tolerance=±5% resistance=220 package=THT]
  S1 = Pushbutton [package="[THT]"]
  S2 = Pushbutton [package="[THT]"]
  LED1 = LED - 5mm [color="Red (633nm)" package="5 mm [THT]"]

nets:
  N1: Part1.5V, R1.Pin_0
  N2: Part1.GND, LED1.cathode
  N3: R1.Pin_1, S1.Pin_3, S1.Pin_4, S2.Pin_3, S2.Pin_4, LED1.anode
  N4: S1.Pin_1, S1.Pin_2
  N5: S2.Pin_1, S2.Pin_2
