# Fritzing sketch resistor_ladder_example (saved by Fritzing 0.9.0b)
breadboards: 1

parts:
  Part1 = Arduino Uno (Rev3)
  J1 = Piezo Speaker
  S1 = Pushbutton [package="[THT]"]
  S2 = Pushbutton [package="[THT]"]
  S3 = Pushbutton [package="[THT]"]
  S4 = Pushbutton [package="[THT]"]
  R1 = Resistor [tolerance=±5% resistance=220 package=THT]
  R2 = Resistor [tolerance=±5% resistance=10k package=THT]
  R3 = Resistor [tolerance=±5% resistance=1M package=THT]
  R4 = Resistor [tolerance=±5% resistance=220 package=THT]

nets:
  N1: Part1.A0, Part1.5V, S1.Pin_3, S1.Pin_4, S2.Pin_3, S2.Pin_4, S3.Pin_3, S3.Pin_4, S4.Pin_3, S4.Pin_4, R1.Pin_0, R1.Pin_1, R2.Pin_0, R2.Pin_1, R3.Pin_0, R3.Pin_1, R4.Pin_1
  N2: Part1.D8, J1.pin2
  N3: Part1.GND, J1.pin1, R4.Pin_0
  N4: S1.Pin_1, S1.Pin_2
  N5: S2.Pin_1, S2.Pin_2
  N6: S3.Pin_1, S3.Pin_2
  N7: S4.Pin_1, S4.Pin_2
